# Fritzing sketch hardware circuitry (saved by Fritzing 1.0.4)
breadboards: 1

parts:
  Part1 = Arduino Uno (Rev3)
  Part2 = InvenSense MPU6050
  J1 = Basic Servo
  J2 = Basic Servo
  VCC1 = Battery block 9V [internal_resistance=0.1Ω]

nets:
  N1: Part1.A4/SDA, Part2.SDA
  N2: Part1.A5/SCL, Part2.SCL
  N3: Part1.D10_PWM/SS, J1.pulse
  VCC: Part1.5V, Part2.VCC, J1.vcc
  GND: Part1.GND, Part2.GND, J1.gnd, J2.gnd, VCC1.-
  N4: Part1.VIN, VCC1.+
